# Fritzing sketch MotorBoard (saved by Fritzing 0.9.3b)
circuit board: 6.5cm x 7cm
breadboards: 1

parts:
  C1 = Electrolytic Capacitor [capacitance=1000µF package="300 mil [THT, electrolytic]"]
  Arduino_Mini_Pro = Arduino Pro Mini v13
  DR_B-EN = female pin header, 8 pins [form="♀ (female)"]
  part = female pin header, 8 pins [form="♀ (female)"]
  part_2 = female pin header, 8 pins [form="♀ (female)"]
  DR_A-EN = female pin header, 8 pins [form="♀ (female)"]
  GND/12V = Screw terminal - 2 pins [package=THT]
  DR_B_B2/B1/A2/A1 = female pin header, 4 pins [form="♀ (female)"]
  DR_A_B2/B1/A2/A1 = female pin header, 4 pins [form="♀ (female)"]
  D1 = Rectifier Diode [part_number=1N4001 package="300 mil [THT]"]
  GND/5V = Screw terminal - 2 pins [package=THT]
  SPI = female pin header, 4 pins [form="♀ (female)"]

nets:
  N1: C1.-, DR_B-EN.pin2, part_2.pin2, GND/12V.pin1
  N2: C1.+, DR_B-EN.pin1, part_2.pin1, GND/12V.pin2
  N3: Arduino_Mini_Pro.RAW, DR_B-EN.pin7, part_2.pin7, D1.cathode
  N4: Arduino_Mini_Pro.GND, DR_B-EN.pin8, part_2.pin8, GND/5V.pin1
  N5: Arduino_Mini_Pro.A1, part.pin1
  N6: Arduino_Mini_Pro.A0, DR_A-EN.pin1
  N7: Arduino_Mini_Pro.D13/SCK, SPI.pin3
  N8: Arduino_Mini_Pro.D12/MISO, SPI.pin2
  N9: Arduino_Mini_Pro.D11_PWM/MOSI, SPI.pin1
  N10: Arduino_Mini_Pro.D10_PWM/SS, SPI.pin4
  N11: Arduino_Mini_Pro.D8, part.pin2, DR_A-EN.pin2
  N12: Arduino_Mini_Pro.D7, part.pin3, DR_A-EN.pin3
  N13: Arduino_Mini_Pro.D6_PWM, part.pin4, DR_A-EN.pin4
  N14: Arduino_Mini_Pro.D5_PWM, part.pin7
  N15: Arduino_Mini_Pro.D4, part.pin8
  N16: Arduino_Mini_Pro.D3_PWM, DR_A-EN.pin7
  N17: Arduino_Mini_Pro.D2, DR_A-EN.pin8
  N18: DR_B-EN.pin3, DR_B_B2/B1/A2/A1.pin1
  N19: DR_B-EN.pin4, DR_B_B2/B1/A2/A1.pin2
  N20: DR_B-EN.pin5, DR_B_B2/B1/A2/A1.pin3
  N21: DR_B-EN.pin6, DR_B_B2/B1/A2/A1.pin4
  N22: part.pin5, part.pin6
  N23: part_2.pin3, DR_A_B2/B1/A2/A1.pin1
  N24: part_2.pin4, DR_A_B2/B1/A2/A1.pin2
  N25: part_2.pin5, DR_A_B2/B1/A2/A1.pin3
  N26: part_2.pin6, DR_A_B2/B1/A2/A1.pin4
  N27: DR_A-EN.pin5, DR_A-EN.pin6
  N28: D1.anode, GND/5V.pin2

notes:
  SS/SCK/MISO/MOSI
  TSC
  Motorboard
  W. Birkfellner
  2017-V1.1
